# Fritzing sketch Example3 (saved by Fritzing 0.9.2b)
breadboards: 1

parts:
  R2 = Rotary Potentiometer (Small) [maximum_resistance=10kΩ package=THT]
  R3 = Resistor [tolerance=±5% resistance=220 package=THT]
  R4 = Resistor [tolerance=±5% resistance=220 package=THT]
  LED1 = LED - 5mm [color="Red (633nm)" package="5 mm [THT]"]
  LED2 = LED - 5mm [color="Red (633nm)" package="5 mm [THT]"]
  R5 = Photocell (LDR) [package=THT]
  R6 = Resistor [tolerance=±5% resistance=220 package=THT]
  R7 = Resistor [tolerance=±5% resistance=220 package=THT]
  LED3 = LED - 5mm [color="Red (633nm)" package="5 mm [THT]"]

nets:
  GND: R2.leg1, LED1.cathode, LED2.cathode, R5.pin_0, LED3.cathode
  N1: R2.wiper, LED2.anode
  5V: R2.leg2, R3.Pin_0, R6.Pin_1
  N2: R3.Pin_1, R4.Pin_0
  N3: R4.Pin_1, LED1.anode
  N4: R5.pin_1, R6.Pin_0, R7.Pin_0
  N5: R7.Pin_1, LED3.anode

notes:
  Example 1
  Example 2
  Example 3
