# Fritzing sketch Example5 (saved by Fritzing 0.9.2b)
breadboards: 1

parts:
  S1 = Toggle Switch [package=THT]
  R1 = Resistor [tolerance=±5% resistance=47k package=THT]
  C1 = Electrolytic Capacitor [capacitance=4.7mF voltage=20V package="100 mil [THT, electrolytic]"]

nets:
  5V: S1.L1
  N1: S1.COM, R1.Pin_0
  GND: S1.L2, C1.-
  N2: R1.Pin_1, C1.+

notes:
  Source: http://reviseomatic.org/help/s-capacitors/Capacitors%20-%20RC%20Timing.php
