# Fritzing sketch Example2 (saved by Fritzing 0.9.2b)
breadboards: 1

parts:
  S1 = Pushbutton [package=THT]
  VCC1 = Battery
  R1 = Resistor [tolerance=±5% resistance=220 package=THT]
  LED1 = LED - 5mm [color="Red (633nm)" package="5 mm [THT]"]
  R2 = Photocell (LDR) [package=THT]
  R3 = Resistor [tolerance=±5% resistance=220 package=THT]

nets:
  N1: S1.leg0, R1.Pin_0
  3V: S1.leg1, VCC1.+, R3.Pin_0
  GND: VCC1.-, LED1.cathode, R2.pin_1
  N2: R1.Pin_1, LED1.anode
  N3: R2.pin_0, R3.Pin_1
