# Fritzing sketch Example1 (saved by Fritzing 0.9.2b)
breadboards: 1

parts:
  S1 = Momentary Switch [package=ksa_sealed_tac_switch]
  R1 = Resistor [tolerance=±5% resistance=220 package=THT]
  LED1 = LED - 5mm [color="Red (633nm)" package="5 mm [THT]"]
  S2 = Toggle Switch [package=THT]
  LED2 = LED - 5mm [color="Red (633nm)" package="5 mm [THT]"]
  LED3 = LED - 5mm [color="Red (633nm)" package="5 mm [THT]"]
  R2 = Resistor [tolerance=±5% resistance=220 package=THT]
  R3 = Resistor [tolerance=±5% resistance=220 package=THT]

nets:
  5V: S1.1, S1.2, S2.COM
  N1: S1.3, S1.4, R1.Pin_0
  N2: R1.Pin_1, LED1.anode
  GND: LED1.cathode, LED2.cathode, LED3.cathode
  N3: S2.L1, R2.Pin_0
  N4: S2.L2, R3.Pin_0
  N5: LED2.anode, R3.Pin_1
  N6: LED3.anode, R2.Pin_1

notes:
  Example 1
  Example 2
  Circuits 1 Lab Demonstrations
