# Fritzing sketch Example4 (saved by Fritzing 0.9.2b)
breadboards: 1

parts:
  R1 = Resistor [tolerance=±5% resistance=220 package=THT]
  R3 = Rotary Potentiometer (Small) [maximum_resistance=100kΩ package=THT]
  J1 = Basic Force Sensing Resistor (FSR) [package=THT]
  R2 = Resistor [tolerance=±5% resistance=220 package=THT]
  VCC1 = Battery

nets:
  Vmm+: R1.Pin_0, R2.Pin_0
  N1: R1.Pin_1, R3.leg2, VCC1.+
  Vmm-: R3.wiper, J1.pin_1
  N2: J1.pin_0, R2.Pin_1, VCC1.-

notes:
  Source http://www.electronicshub.org/wheatstone-bridge/
  Source: http://www.electronicshub.org/wheatstone-bridge/
