# Fritzing sketch Example7 (saved by Fritzing 0.9.2b)
breadboards: 1

parts:
  VCC1 = Battery
  R1 = Resistor [tolerance=±5% resistance=220 package=THT]
  L1 = Inductor [inductance=10mH package="400 mil [THT]"]
  S1 = Pushbutton [package=THT]

nets:
  N1: VCC1.-, S1.leg0
  N2: VCC1.+, R1.Pin_0
  N3: R1.Pin_1, L1.pin_0
  Break Connection And Put Meter Here: L1.pin_1, S1.leg1
